# Fritzing sketch FanController2 (saved by Fritzing 0.9.3b)
breadboards: 1

parts:
  Part1 = Arduino Nano (Rev3.0)
  R1 = Resistor [tolerance=±5% resistance=10k package=THT]
  R2 = Resistor [tolerance=±5% resistance=10k package=THT]
  R3 = Resistor [tolerance=±5% resistance=680 package=THT]
  Q1 = NPN-Transistor [package="TO92 [THT]"]
  J1 = Peltier Element
  LCD2 = LCD screen
  LCM1602_IIC1 = LCM1602 IIC [part_number="LCM1602 IIC" chip_label="LCM1602 IIC" package="DIP (Dual Inline) [THT]"]
  920KV_Motor1 = DJI 920 KV Motor
  M1 = ESC
  Power_plug1 = Power plug
  U2 = LM2596 step down module
  J2 = Piezo Speaker

nets:
  GND: Part1.GND, Q1.E, J1.pin1, LCM1602_IIC1.GND, M1.GND, Power_plug1.GND, U2.IN-, U2.OUT-
  N1: Part1.D9, Q1.B
  N2: Part1.D10, J2.pin2
  VIN: Part1.VIN, LCM1602_IIC1.VCC, M1.5V, U2.OUT+
  N3: Part1.5V, R1.Pin_0, R2.Pin_0
  N4: Part1.A5, LCM1602_IIC1.SCL
  N5: Part1.A4, LCM1602_IIC1.SDA
  N6: Part1.A0, R3.Pin_0, J1.pin2
  N7: R1.Pin_1, R2.Pin_1, R3.Pin_1
  N8: Q1.C, M1.DATA
  VSS: LCD2.VSS, LCM1602_IIC1.VSS
  VDD: LCD2.VDD, LCM1602_IIC1.VDD
  N9: LCD2.V0, LCM1602_IIC1.V0
  N10: LCD2.RS, LCM1602_IIC1.RS
  N11: LCD2.R/W, LCM1602_IIC1.RW
  N12: LCD2.E, LCM1602_IIC1.E
  N13: LCD2.DB0, LCM1602_IIC1.D0
  N14: LCD2.DB1, LCM1602_IIC1.D1
  N15: LCD2.DB2, LCM1602_IIC1.D2
  N16: LCD2.DB3, LCM1602_IIC1.D3
  N17: LCD2.DB4, LCM1602_IIC1.D4
  N18: LCD2.DB5, LCM1602_IIC1.D5
  N19: LCD2.DB6, LCM1602_IIC1.D6
  N20: LCD2.DB7, LCM1602_IIC1.D7
  N21: LCD2.LED+, LCM1602_IIC1.A
  N22: LCD2.LED-, LCM1602_IIC1.K
  N23: LCM1602_IIC1.LED_A, LCM1602_IIC1.LED_B
  N24: 920KV_Motor1.w, M1.W
  N25: 920KV_Motor1.v, M1.V
  N26: 920KV_Motor1.u, M1.U
  N27: Power_plug1.VCC, U2.IN+

custom parts:
  LCM1602 IIC: I2C-Module to use a 1602 or 2004 LCD on with the wire.h libory Serial LCD Modul
  DJI 920 KV Motor: DJI Brushless Outrunner 2212/920K Motor F330-550
  LM2596 step down module: LM2596 DC-DC step down power supply module 3 A.
